# Fritzing sketch arm robot pcb (saved by Fritzing 0.9.3b)
breadboards: 1

parts:
  JACK1 = 2.1mm Barrel Jack with Terminal Block
  U1 = ESP32-38PinWide [part_number=ESP32-38PinWide]
  J1 = Basic Servo
  J2 = Basic Servo
  J3 = Basic Servo
  SERVO1 = Tower Pro SG90 servo [part_number=101246]
  M1 = fc-51 [package=THT]

nets:
  VCC: JACK1.POS, J1.vcc, J2.vcc, J3.vcc, M1.pin3
  GND: JACK1.NEG, U1.GPIO11, J1.gnd, J2.gnd, J3.gnd, M1.pin2
  N1: U1.3.3, SERVO1.+5V
  N2: U1.GPIO25, SERVO1.Signal
  N3: U1.GPIO26, J3.pulse
  N4: U1.GPIO27, J2.pulse
  N5: U1.GPIO14, J1.pulse
  N6: U1.GPIO12, M1.pin1
  GND_2: U1.GND, SERVO1.GND

custom parts:
  ESP32-38PinWide: Generic 38-Pin ESP32 with wide format (only access to one side of pins on a breadboard) based on Stephen Lilley's HiLetgo ESP-WROOM-32 ESP32 ESP-32S Development Board.
  Tower Pro SG90 servo: Original file by John De Cristofaro http://www.adafruit.com/products/1449 Adafruit Feedback Servo (Small) Edited by: e-radionica.com 28/9/2015
